// Logisim project Diagram_logisim.circ as structural Verilog: 1 circuit, main circuit main
module main (
  input  B0,
  input  in_2,
  input  A1,
  input  B1,
  input  A2,
  input  B2,
  output S0,
  output S1,
  output S2,
  output S3
);

  wire and_1_out, and_2_out, and_3_out, and_4_out, and_5_out, or_1_out, xor_1_out, xor_2_out;

  xor xor_1 (xor_1_out, A1, B1);
  xor xor_2 (xor_2_out, A2, B2);
  xor xor_3 (S0, B0, in_2);
  and and_1 (and_1_out, B0, in_2);
  and and_2 (and_2_out, and_1_out, xor_1_out);
  and and_3 (and_3_out, A1, B1);
  and and_4 (and_4_out, or_1_out, xor_2_out);
  and and_5 (and_5_out, A2, B2);
  xor xor_4 (S1, xor_1_out, and_1_out);
  or or_1 (or_1_out, and_2_out, and_3_out);
  xor xor_5 (S2, xor_2_out, or_1_out);
  or or_2 (S3, and_4_out, and_5_out);

  // Notes on the sheet:
  //   A0
  //   a1
  //   a2
  //   b0
  //   b1
  //   b2
  //   d1
  //   d2
  //   C1
endmodule
